// Logisim project 60_Up_Down_Counter.circ as structural Verilog: 4 circuits, main circuit main
module main (
  input  Up_Down_Toggle
);

  wire clock_1_out, dec_7seg_driver_1_a, dec_7seg_driver_1_b, dec_7seg_driver_1_c, dec_7seg_driver_1_d,
       dec_7seg_driver_1_e, dec_7seg_driver_1_f, dec_7seg_driver_1_g, dec_7seg_driver_2_a,
       dec_7seg_driver_2_b, dec_7seg_driver_2_c, dec_7seg_driver_2_d, dec_7seg_driver_2_e,
       dec_7seg_driver_2_f, dec_7seg_driver_2_g, n6_counter_1_a, n6_counter_1_b, n6_counter_1_c,
       n10_counter_1_a, n10_counter_1_b, n10_counter_1_c, n10_counter_1_d, n10_counter_1_is_9_or_0;

  _6_Counter u_6_counter_1 (
    .up_down(Up_Down_Toggle), .Clock(n10_counter_1_is_9_or_0), .A(n6_counter_1_a), .B(n6_counter_1_b),
    .C(n6_counter_1_c));
  Clock clock_1 (.out(clock_1_out));
  _10_Counter u_10_counter_1 (
    .up_down(Up_Down_Toggle), .Clock(clock_1_out), .Is_9_or_0(n10_counter_1_is_9_or_0), .A(n10_counter_1_a),
    .B(n10_counter_1_b), .C(n10_counter_1_c), .D(n10_counter_1_d));
  dec_7seg_driver dec_7seg_driver_1 (
    .w(1'b0), .x(n6_counter_1_a), .y(n6_counter_1_b), .z(n6_counter_1_c), .a(dec_7seg_driver_1_a),
    .b(dec_7seg_driver_1_b), .c(dec_7seg_driver_1_c), .d(dec_7seg_driver_1_d), .e(dec_7seg_driver_1_e),
    .f(dec_7seg_driver_1_f), .g(dec_7seg_driver_1_g));
  _7_Segment_Display u_7_segment_display_1 (
    .g(dec_7seg_driver_1_g), .f(dec_7seg_driver_1_f), .a(dec_7seg_driver_1_a), .b(dec_7seg_driver_1_b),
    .e(dec_7seg_driver_1_e), .d(dec_7seg_driver_1_d), .c(dec_7seg_driver_1_c));  // open: dp
  dec_7seg_driver dec_7seg_driver_2 (
    .w(n10_counter_1_a), .x(n10_counter_1_b), .y(n10_counter_1_c), .z(n10_counter_1_d),
    .a(dec_7seg_driver_2_a), .b(dec_7seg_driver_2_b), .c(dec_7seg_driver_2_c), .d(dec_7seg_driver_2_d),
    .e(dec_7seg_driver_2_e), .f(dec_7seg_driver_2_f), .g(dec_7seg_driver_2_g));
  _7_Segment_Display u_7_segment_display_2 (
    .g(dec_7seg_driver_2_g), .f(dec_7seg_driver_2_f), .a(dec_7seg_driver_2_a), .b(dec_7seg_driver_2_b),
    .e(dec_7seg_driver_2_e), .d(dec_7seg_driver_2_d), .c(dec_7seg_driver_2_c));  // open: dp
endmodule

module dec_7seg_driver (
  input  w,
  input  x,
  input  y,
  input  z,
  output a,
  output b,
  output c,
  output d,
  output e,
  output f,
  output g
);

  wire and_1_out, and_2_out, and_3_out, and_4_out, and_5_out, and_6_out, and_7_out, and_8_out, and_9_out,
       and_10_out, and_11_out, and_12_out, and_13_out, and_14_out, not_1_out, not_2_out, not_3_out, not_4_out;

  not not_1 (not_1_out, w);
  not not_2 (not_2_out, x);
  not not_3 (not_3_out, y);
  not not_4 (not_4_out, z);
  and and_1 (and_1_out, x, z);
  and and_2 (and_2_out, not_2_out, not_4_out);
  and and_3 (and_3_out, not_3_out, not_4_out);
  and and_4 (and_4_out, y, z);
  and and_5 (and_5_out, not_2_out, not_4_out);
  and and_6 (and_6_out, not_2_out, y);
  and and_7 (and_7_out, y, not_4_out);
  and and_8 (and_8_out, x, not_3_out, z);
  and and_9 (and_9_out, not_2_out, not_4_out);
  and and_10 (and_10_out, y, not_4_out);
  and and_11 (and_11_out, not_3_out, not_4_out);
  and and_12 (and_12_out, x, not_3_out);
  and and_13 (and_13_out, not_2_out, y);
  and and_14 (and_14_out, y, not_4_out);
  or or_1 (a, w, y, and_1_out, and_2_out);
  or or_2 (b, not_2_out, and_3_out, and_4_out);
  or or_3 (c, x, not_3_out, z);
  or or_4 (d, w, and_5_out, and_6_out, and_7_out, and_8_out);
  or or_5 (e, and_9_out, and_10_out);
  or or_6 (f, w, x, and_11_out);
  or or_7 (g, w, and_12_out, and_13_out, and_14_out);
endmodule

module _10_Counter (
  input  Clock,
  input  up_down,
  output A,
  output B,
  output C,
  output D,
  output Is_9_or_0
);

  wire and_1_out, and_2_out, and_3_out, and_4_out, and_5_out, and_6_out, and_7_out, and_8_out, and_9_out,
       and_10_out, and_11_out, and_12_out, and_13_out, and_14_out, and_15_out, and_16_out, and_17_out,
       and_18_out, and_19_out, and_20_out, and_21_out, and_22_out, and_23_out, d_ff_1_qn, d_ff_2_qn,
       d_ff_3_qn, d_ff_4_qn, not_1_out, not_2_out, not_3_out, not_5_out, not_6_out, not_7_out, not_8_out,
       or_1_out, or_2_out, or_3_out, or_4_out, or_5_out, or_6_out, or_7_out, or_8_out, or_9_out, or_10_out;

  not not_1 (not_1_out, up_down);
  and and_1 (and_1_out, A, D);
  and and_2 (and_2_out, A, d_ff_4_qn);
  and and_3 (and_3_out, B, C, D);
  and and_4 (and_4_out, B, D);
  and and_5 (and_5_out, B, C);
  and and_6 (and_6_out, A, d_ff_4_qn);
  and and_7 (and_7_out, B, d_ff_4_qn);
  and and_8 (and_8_out, B, d_ff_3_qn);
  and and_9 (and_9_out, d_ff_2_qn, C, D);
  and and_10 (and_10_out, A, d_ff_4_qn);
  and and_11 (and_11_out, D, C);
  and and_12 (and_12_out, B, d_ff_3_qn, d_ff_4_qn);
  and and_13 (and_13_out, C, d_ff_4_qn);
  and and_14 (and_14_out, d_ff_1_qn, d_ff_3_qn, D);
  and and_15 (and_15_out, d_ff_1_qn, d_ff_2_qn, d_ff_3_qn, d_ff_4_qn);
  and and_16 (and_16_out, up_down, or_1_out);
  or or_1 (or_1_out, and_1_out, and_15_out);
  and and_17 (and_17_out, not_1_out, or_2_out);
  or or_2 (or_2_out, and_2_out, and_3_out);
  or or_3 (or_3_out, and_4_out, and_5_out, and_6_out);
  or or_4 (or_4_out, and_8_out, and_9_out, and_7_out);
  or or_5 (or_5_out, and_10_out, and_11_out, and_12_out);
  or or_6 (or_6_out, and_13_out, and_14_out);
  or or_7 (or_7_out, and_16_out, and_17_out);
  and and_18 (and_18_out, up_down, or_3_out);
  or or_8 (or_8_out, and_18_out, and_19_out);
  and and_19 (and_19_out, not_1_out, or_4_out);
  and and_20 (and_20_out, up_down, or_5_out);
  or or_9 (or_9_out, and_20_out, and_21_out);
  and and_21 (and_21_out, not_1_out, or_6_out);
  D_Flip_Flop d_ff_1 (.clk(Clock), .D(or_7_out), .Q(A), .Qn(d_ff_1_qn));  // open: preset, en, reset
  D_Flip_Flop d_ff_2 (.clk(Clock), .D(or_8_out), .Q(B), .Qn(d_ff_2_qn));  // open: preset, en, reset
  D_Flip_Flop d_ff_3 (.clk(Clock), .D(or_9_out), .Q(C), .Qn(d_ff_3_qn));  // open: preset, en, reset
  D_Flip_Flop d_ff_4 (.clk(Clock), .D(d_ff_4_qn), .Q(D), .Qn(d_ff_4_qn));  // open: preset, en, reset
  not not_2 (not_2_out, B);
  not not_3 (not_3_out, C);
  and and_22 (and_22_out, not_1_out, D, not_3_out, not_2_out, A);
  or or_10 (or_10_out, and_22_out, and_23_out);
  not not_4 (Is_9_or_0, or_10_out);
  not not_5 (not_5_out, D);
  not not_6 (not_6_out, C);
  not not_7 (not_7_out, B);
  not not_8 (not_8_out, A);
  and and_23 (and_23_out, not_8_out, not_7_out, not_6_out, not_5_out, up_down);
endmodule

module _6_Counter (
  input  Clock,
  input  up_down,
  output A,
  output B,
  output C
);

  wire and_1_out, and_2_out, and_3_out, and_4_out, and_5_out, and_6_out, and_7_out, and_8_out, and_9_out,
       and_10_out, and_11_out, and_12_out, d_ff_1_qn, d_ff_2_qn, d_ff_3_qn, not_1_out, or_1_out, or_2_out,
       or_3_out, or_4_out, or_5_out, or_6_out;

  not not_1 (not_1_out, up_down);
  and and_1 (and_1_out, A, d_ff_3_qn);
  and and_2 (and_2_out, B, C);
  and and_3 (and_3_out, A, C);
  and and_4 (and_4_out, d_ff_1_qn, d_ff_2_qn, d_ff_3_qn);
  and and_5 (and_5_out, A, d_ff_3_qn);
  and and_6 (and_6_out, B, C);
  and and_7 (and_7_out, B, d_ff_3_qn);
  and and_8 (and_8_out, d_ff_1_qn, d_ff_2_qn, C);
  and and_9 (and_9_out, not_1_out, or_1_out);
  or or_1 (or_1_out, and_1_out, and_2_out);
  and and_10 (and_10_out, up_down, or_2_out);
  or or_2 (or_2_out, and_3_out, and_4_out);
  or or_3 (or_3_out, and_5_out, and_6_out);
  or or_4 (or_4_out, and_8_out, and_7_out);
  or or_5 (or_5_out, and_9_out, and_10_out);
  and and_11 (and_11_out, up_down, or_3_out);
  or or_6 (or_6_out, and_11_out, and_12_out);
  and and_12 (and_12_out, not_1_out, or_4_out);
  D_Flip_Flop d_ff_1 (.clk(Clock), .D(or_5_out), .Q(A), .Qn(d_ff_1_qn));  // open: preset, en, reset
  D_Flip_Flop d_ff_2 (.clk(Clock), .D(or_6_out), .Q(B), .Qn(d_ff_2_qn));  // open: preset, en, reset
  D_Flip_Flop d_ff_3 (.clk(Clock), .D(d_ff_3_qn), .Q(C), .Qn(d_ff_3_qn));  // open: preset, en, reset
endmodule
