// Logisim project Normal_Inputs.circ as structural Verilog: 6 circuits, main circuit main
module main (
  input  in_1,
  input  Number_1,
  input  in_3,
  input  in_4,
  input  in_5,
  input  Number_2,
  input  in_7,
  input  in_8
);

  wire adder_1_carry, adder_1_out_9, adder_1_out_10, adder_1_out_11, adder_1_out_12, dec_7seg_driver_1_a,
       dec_7seg_driver_1_b, dec_7seg_driver_1_c, dec_7seg_driver_1_d, dec_7seg_driver_1_e,
       dec_7seg_driver_1_f, dec_7seg_driver_1_g, dec_7seg_driver_2_a, dec_7seg_driver_2_b,
       dec_7seg_driver_2_c, dec_7seg_driver_2_d, dec_7seg_driver_2_e, dec_7seg_driver_2_f,
       dec_7seg_driver_2_g, dec_7seg_driver_3_a, dec_7seg_driver_3_b, dec_7seg_driver_3_c,
       dec_7seg_driver_3_d, dec_7seg_driver_3_e, dec_7seg_driver_3_f, dec_7seg_driver_3_g,
       dec_7seg_driver_4_a, dec_7seg_driver_4_b, dec_7seg_driver_4_c, dec_7seg_driver_4_d,
       dec_7seg_driver_4_e, dec_7seg_driver_4_f, dec_7seg_driver_4_g, dec_7seg_driver_5_a,
       dec_7seg_driver_5_b, dec_7seg_driver_5_c, dec_7seg_driver_5_d, dec_7seg_driver_5_e,
       dec_7seg_driver_5_f, dec_7seg_driver_5_g, dec_7seg_driver_6_a, dec_7seg_driver_6_b,
       dec_7seg_driver_6_c, dec_7seg_driver_6_d, dec_7seg_driver_6_e, dec_7seg_driver_6_f,
       dec_7seg_driver_6_g, ones_1_w, ones_1_x, ones_1_y, ones_1_z, ones_2_w, ones_2_x, ones_2_y, ones_2_z,
       ones_3_w, ones_3_x, ones_3_y, ones_3_z, tens_1_f1, tens_2_f1, tens_3_f1, tens_3_f2;

  Tens tens_1 (.in_1(1'b0), .in_2(in_1), .in_3(Number_1), .in_4(in_3), .in_5(in_4), .f1(tens_1_f1));  // open: f2
  _7_Segment_Display u_7_segment_display_1 (
    .g(dec_7seg_driver_1_g), .f(dec_7seg_driver_1_f), .a(dec_7seg_driver_1_a), .b(dec_7seg_driver_1_b),
    .e(dec_7seg_driver_1_e), .d(dec_7seg_driver_1_d), .c(dec_7seg_driver_1_c));  // open: dp
  dec_7seg_driver dec_7seg_driver_1 (
    .w(1'b0), .x(1'b0), .y(1'b0), .z(tens_1_f1), .a(dec_7seg_driver_1_a), .b(dec_7seg_driver_1_b),
    .c(dec_7seg_driver_1_c), .d(dec_7seg_driver_1_d), .e(dec_7seg_driver_1_e), .f(dec_7seg_driver_1_f),
    .g(dec_7seg_driver_1_g));
  Adder adder_1 (
    .in_1(in_1), .in_2(Number_1), .in_3(in_3), .in_4(in_4), .in_5(in_5), .in_6(Number_2), .in_7(in_7),
    .in_8(in_8), .out_9(adder_1_out_9), .out_10(adder_1_out_10), .out_11(adder_1_out_11),
    .out_12(adder_1_out_12), .carry(adder_1_carry));
  _7_Segment_Display u_7_segment_display_2 (
    .g(dec_7seg_driver_2_g), .f(dec_7seg_driver_2_f), .a(dec_7seg_driver_2_a), .b(dec_7seg_driver_2_b),
    .e(dec_7seg_driver_2_e), .d(dec_7seg_driver_2_d), .c(dec_7seg_driver_2_c));  // open: dp
  dec_7seg_driver dec_7seg_driver_2 (
    .w(ones_1_w), .x(ones_1_x), .y(ones_1_y), .z(ones_1_z), .a(dec_7seg_driver_2_a), .b(dec_7seg_driver_2_b),
    .c(dec_7seg_driver_2_c), .d(dec_7seg_driver_2_d), .e(dec_7seg_driver_2_e), .f(dec_7seg_driver_2_f),
    .g(dec_7seg_driver_2_g));
  Ones ones_1 (
    .c_out(1'b0), .s4(in_1), .s3(Number_1), .s2(in_3), .s1(in_4), .w(ones_1_w), .x(ones_1_x), .y(ones_1_y),
    .z(ones_1_z));
  dec_7seg_driver dec_7seg_driver_3 (
    .w(1'b0), .x(1'b0), .y(1'b0), .z(tens_2_f1), .a(dec_7seg_driver_3_a), .b(dec_7seg_driver_3_b),
    .c(dec_7seg_driver_3_c), .d(dec_7seg_driver_3_d), .e(dec_7seg_driver_3_e), .f(dec_7seg_driver_3_f),
    .g(dec_7seg_driver_3_g));
  Tens tens_2 (.in_1(1'b0), .in_2(in_5), .in_3(Number_2), .in_4(in_7), .in_5(in_8), .f1(tens_2_f1));  // open: f2
  _7_Segment_Display u_7_segment_display_3 (
    .g(dec_7seg_driver_3_g), .f(dec_7seg_driver_3_f), .a(dec_7seg_driver_3_a), .b(dec_7seg_driver_3_b),
    .e(dec_7seg_driver_3_e), .d(dec_7seg_driver_3_d), .c(dec_7seg_driver_3_c));  // open: dp
  _7_Segment_Display u_7_segment_display_4 (
    .g(dec_7seg_driver_4_g), .f(dec_7seg_driver_4_f), .a(dec_7seg_driver_4_a), .b(dec_7seg_driver_4_b),
    .e(dec_7seg_driver_4_e), .d(dec_7seg_driver_4_d), .c(dec_7seg_driver_4_c));  // open: dp
  dec_7seg_driver dec_7seg_driver_4 (
    .w(ones_2_w), .x(ones_2_x), .y(ones_2_y), .z(ones_2_z), .a(dec_7seg_driver_4_a), .b(dec_7seg_driver_4_b),
    .c(dec_7seg_driver_4_c), .d(dec_7seg_driver_4_d), .e(dec_7seg_driver_4_e), .f(dec_7seg_driver_4_f),
    .g(dec_7seg_driver_4_g));
  Ones ones_2 (
    .c_out(1'b0), .s4(in_5), .s3(Number_2), .s2(in_7), .s1(in_8), .w(ones_2_w), .x(ones_2_x), .y(ones_2_y),
    .z(ones_2_z));
  Tens tens_3 (
    .in_1(adder_1_carry), .in_2(adder_1_out_12), .in_3(adder_1_out_11), .in_4(adder_1_out_10),
    .in_5(adder_1_out_9), .f2(tens_3_f2), .f1(tens_3_f1));
  dec_7seg_driver dec_7seg_driver_5 (
    .w(1'b0), .x(1'b0), .y(tens_3_f2), .z(tens_3_f1), .a(dec_7seg_driver_5_a), .b(dec_7seg_driver_5_b),
    .c(dec_7seg_driver_5_c), .d(dec_7seg_driver_5_d), .e(dec_7seg_driver_5_e), .f(dec_7seg_driver_5_f),
    .g(dec_7seg_driver_5_g));
  _7_Segment_Display u_7_segment_display_5 (
    .g(dec_7seg_driver_6_g), .f(dec_7seg_driver_6_f), .a(dec_7seg_driver_6_a), .b(dec_7seg_driver_6_b),
    .e(dec_7seg_driver_6_e), .d(dec_7seg_driver_6_d), .c(dec_7seg_driver_6_c));  // open: dp
  _7_Segment_Display u_7_segment_display_6 (
    .g(dec_7seg_driver_5_g), .f(dec_7seg_driver_5_f), .a(dec_7seg_driver_5_a), .b(dec_7seg_driver_5_b),
    .e(dec_7seg_driver_5_e), .d(dec_7seg_driver_5_d), .c(dec_7seg_driver_5_c));  // open: dp
  dec_7seg_driver dec_7seg_driver_6 (
    .w(ones_3_w), .x(ones_3_x), .y(ones_3_y), .z(ones_3_z), .a(dec_7seg_driver_6_a), .b(dec_7seg_driver_6_b),
    .c(dec_7seg_driver_6_c), .d(dec_7seg_driver_6_d), .e(dec_7seg_driver_6_e), .f(dec_7seg_driver_6_f),
    .g(dec_7seg_driver_6_g));
  Ones ones_3 (
    .c_out(adder_1_carry), .s4(adder_1_out_12), .s3(adder_1_out_11), .s2(adder_1_out_10), .s1(adder_1_out_9),
    .w(ones_3_w), .x(ones_3_x), .y(ones_3_y), .z(ones_3_z));

  // Notes on the sheet:
  //   +
  //   =
endmodule

module dec_7seg_driver (
  input  w,
  input  x,
  input  y,
  input  z,
  output a,
  output b,
  output c,
  output d,
  output e,
  output f,
  output g
);

  wire and_1_out, and_2_out, and_3_out, and_4_out, and_5_out, and_6_out, and_7_out, and_8_out, and_9_out,
       and_10_out, and_11_out, and_12_out, and_13_out, and_14_out, not_1_out, not_2_out, not_3_out, not_4_out;

  not not_1 (not_1_out, x);
  not not_2 (not_2_out, w);
  not not_3 (not_3_out, y);
  not not_4 (not_4_out, z);
  and and_1 (and_1_out, x, z);
  and and_2 (and_2_out, not_1_out, not_4_out);
  and and_3 (and_3_out, not_3_out, not_4_out);
  and and_4 (and_4_out, y, z);
  and and_5 (and_5_out, not_1_out, not_4_out);
  and and_6 (and_6_out, not_1_out, y);
  and and_7 (and_7_out, y, not_4_out);
  and and_8 (and_8_out, x, not_3_out, z);
  and and_9 (and_9_out, not_1_out, not_4_out);
  and and_10 (and_10_out, y, not_4_out);
  and and_11 (and_11_out, not_3_out, not_4_out);
  and and_12 (and_12_out, x, not_3_out);
  and and_13 (and_13_out, not_1_out, y);
  and and_14 (and_14_out, y, not_4_out);
  or or_1 (a, w, y, and_1_out, and_2_out);
  or or_2 (b, not_1_out, and_3_out, and_4_out);
  or or_3 (c, x, not_3_out, z);
  or or_4 (d, w, and_5_out, and_6_out, and_7_out, and_8_out);
  or or_5 (e, and_9_out, and_10_out);
  or or_6 (f, w, x, and_11_out);
  or or_7 (g, w, and_12_out, and_13_out, and_14_out);
endmodule

module Multiplexer (
  input  s1,
  input  s2,
  input  w,
  input  x,
  input  y,
  input  z,
  input  EN_prime,
  output out_8
);

  wire _00_out, _01_out, _10_out, _11_out, not_1_out, not_2_out, not_3_out;

  not not_1 (not_1_out, s1);
  not not_2 (not_2_out, s2);
  not not_3 (not_3_out, EN_prime);
  and _00 (_00_out, not_2_out, w, not_1_out, not_3_out);
  and _01 (_01_out, not_1_out, x, s2, not_3_out);
  and _10 (_10_out, not_2_out, y, s1, not_3_out);
  and _11 (_11_out, s1, s2, z, not_3_out);
  or or_1 (out_8, _00_out, _01_out, _10_out, _11_out);
endmodule

module Adder (
  input  in_1,
  input  in_2,
  input  in_3,
  input  in_4,
  input  in_5,
  input  in_6,
  input  in_7,
  input  in_8,
  output out_9,
  output out_10,
  output out_11,
  output out_12,
  output carry
);

  wire multiplexer_2_out_8, multiplexer_4_out_8, multiplexer_6_out_8, not_1_out, not_2_out, not_3_out,
       not_4_out, not_5_out, not_6_out, not_7_out;

  Multiplexer multiplexer_1 (
    .w(in_8), .x(in_8), .y(in_4), .z(not_1_out), .s1(in_4), .s2(in_8), .EN_prime(1'b0), .out_8(out_9));
  not not_1 (not_1_out, in_8);
  Multiplexer multiplexer_2 (
    .w(1'b0), .x(1'b0), .y(1'b0), .z(1'b1), .s1(in_4), .s2(in_8), .EN_prime(1'b0), .out_8(multiplexer_2_out_8));
  not not_2 (not_2_out, multiplexer_2_out_8);
  Multiplexer multiplexer_3 (
    .w(multiplexer_2_out_8), .x(not_2_out), .y(not_3_out), .z(multiplexer_2_out_8), .s1(in_3), .s2(in_7),
    .EN_prime(1'b0), .out_8(out_10));
  not not_3 (not_3_out, multiplexer_2_out_8);
  Multiplexer multiplexer_4 (
    .w(1'b0), .x(multiplexer_2_out_8), .y(multiplexer_2_out_8), .z(1'b1), .s1(in_3), .s2(in_7),
    .EN_prime(1'b0), .out_8(multiplexer_4_out_8));
  Multiplexer multiplexer_5 (
    .w(multiplexer_4_out_8), .x(not_4_out), .y(not_5_out), .z(multiplexer_4_out_8), .s1(in_2), .s2(in_6),
    .EN_prime(1'b0), .out_8(out_11));
  not not_4 (not_4_out, multiplexer_4_out_8);
  not not_5 (not_5_out, multiplexer_4_out_8);
  Multiplexer multiplexer_6 (
    .w(1'b0), .x(multiplexer_4_out_8), .y(multiplexer_4_out_8), .z(1'b1), .s1(in_2), .s2(in_6),
    .EN_prime(1'b0), .out_8(multiplexer_6_out_8));
  not not_6 (not_6_out, multiplexer_6_out_8);
  Multiplexer multiplexer_7 (
    .w(multiplexer_6_out_8), .x(not_6_out), .y(not_7_out), .z(multiplexer_6_out_8), .s1(in_1), .s2(in_5),
    .EN_prime(1'b0), .out_8(out_12));
  not not_7 (not_7_out, multiplexer_6_out_8);
  Multiplexer multiplexer_8 (
    .w(1'b0), .x(multiplexer_6_out_8), .y(multiplexer_6_out_8), .z(1'b1), .s1(in_1), .s2(in_5),
    .EN_prime(1'b0), .out_8(carry));

  // Notes on the sheet:
  //   carry
  //   carry
  //   carry
endmodule

module Tens (
  input  in_1,
  input  in_2,
  input  in_3,
  input  in_4,
  input  in_5,
  output f2,
  output f1
);

  wire and_1_out, and_2_out, and_3_out, nand_1_out, not_1_out, not_2_out, not_3_out, not_4_out, not_5_out,
       not_6_out, or_1_out;

  not not_1 (not_1_out, in_3);
  not not_2 (not_2_out, in_4);
  or or_1 (or_1_out, in_2, in_3);
  nand nand_1 (nand_1_out, not_1_out, not_2_out);
  not not_3 (not_3_out, in_1);
  and and_1 (and_1_out, not_3_out, in_2, nand_1_out);
  and and_2 (and_2_out, in_1, not_4_out, not_5_out);
  not not_4 (not_4_out, in_2);
  not not_5 (not_5_out, in_3);
  not not_6 (not_6_out, in_5);
  and and_3 (and_3_out, not_6_out, in_4, in_3, in_2, in_1);
  and and_4 (f2, in_1, or_1_out);
  or or_2 (f1, and_1_out, and_2_out, and_3_out);
endmodule

module Ones (
  input  c_out,
  input  s4,
  input  s3,
  input  s2,
  input  s1,
  output w,
  output x,
  output y,
  output z
);

  wire _1_2_out, _1_out, _2_2_out, _2_out, _3_2_out, _3_out, _4_2_out, _4_out, _5_2_out, _5_out, _6_2_out,
       _6_out, _7_2_out, _7_out, _8_2_out, _8_out, _9_2_out, _9_out, _11_out, _12_out, _13_out, _14_out,
       _15_out, _16_out, _17_out, _18_out, _19_out, _21_out, _22_out, _23_out, _24_out, _25_out, _26_out,
       _27_out, _28_out, _29_out, not_1_out, not_2_out, not_3_out, not_4_out, not_5_out;

  not not_1 (not_1_out, c_out);
  not not_2 (not_2_out, s4);
  not not_3 (not_3_out, s2);
  not not_4 (not_4_out, s3);
  not not_5 (not_5_out, s1);
  // AND_Gate _0 has open pins: in0=not_1_out, in1=not_2_out, in2=not_4_out, in3=not_3_out, in4=not_5_out, out=open
  and _1 (_1_out, not_1_out, not_2_out, not_4_out, not_3_out, s1);
  and _2 (_2_out, not_1_out, not_2_out, not_4_out, s2, not_5_out);
  and _3 (_3_out, not_1_out, not_2_out, not_4_out, s2, s1);
  and _4 (_4_out, not_1_out, not_2_out, s3, not_3_out, not_5_out);
  and _5 (_5_out, not_1_out, not_2_out, s3, not_3_out, s1);
  and _6 (_6_out, not_1_out, not_2_out, s3, s2, not_5_out);
  and _7 (_7_out, not_1_out, not_2_out, s3, s2, s1);
  and _8 (_8_out, not_1_out, s4, not_4_out, not_3_out, not_5_out);
  and _9 (_9_out, not_1_out, s4, not_4_out, not_3_out, s1);
  // AND_Gate _10 has open pins: in0=not_1_out, in1=s4, in2=not_4_out, in3=s2, in4=not_5_out, out=open
  and _11 (_11_out, not_1_out, s4, not_4_out, s2, s1);
  and _12 (_12_out, not_1_out, s4, s3, not_3_out, not_5_out);
  and _13 (_13_out, not_1_out, s4, s3, not_3_out, s1);
  and _14 (_14_out, not_1_out, s4, s3, s2, not_5_out);
  and _15 (_15_out, not_1_out, s4, s3, s2, s1);
  and _16 (_16_out, c_out, not_2_out, not_4_out, not_3_out, not_5_out);
  and _17 (_17_out, c_out, not_2_out, not_4_out, not_3_out, s1);
  and _18 (_18_out, c_out, not_2_out, not_4_out, s2, not_5_out);
  and _19 (_19_out, c_out, not_2_out, not_4_out, s2, s1);
  // AND_Gate _20 has open pins: in0=c_out, in1=not_2_out, in2=s3, in3=not_3_out, in4=not_5_out, out=open
  and _21 (_21_out, c_out, not_2_out, s3, not_3_out, s1);
  and _22 (_22_out, c_out, not_2_out, s3, s2, not_5_out);
  and _23 (_23_out, c_out, not_2_out, s3, s2, s1);
  and _24 (_24_out, c_out, s4, not_4_out, not_3_out, not_5_out);
  and _25 (_25_out, c_out, s4, not_4_out, not_3_out, s1);
  and _26 (_26_out, c_out, s4, not_4_out, s2, not_5_out);
  and _27 (_27_out, c_out, s4, not_4_out, s2, s1);
  and _28 (_28_out, c_out, s4, s3, not_3_out, not_5_out);
  and _29 (_29_out, c_out, s4, s3, not_3_out, s1);
  // AND_Gate _30 has open pins: in0=c_out, in1=s4, in2=s3, in3=s2, in4=not_5_out, out=open
  or _1_2 (_1_2_out, _1_out, _11_out, _21_out);
  or _2_2 (_2_2_out, _2_out, _12_out, _22_out);
  or _3_2 (_3_2_out, _3_out, _13_out, _23_out);
  or _4_2 (_4_2_out, _4_out, _14_out, _24_out);
  or _5_2 (_5_2_out, _5_out, _15_out, _25_out);
  or _6_2 (_6_2_out, _6_out, _16_out, _26_out);
  or _7_2 (_7_2_out, _7_out, _17_out, _27_out);
  or _8_2 (_8_2_out, _8_out, _18_out, _28_out);
  or _9_2 (_9_2_out, _9_out, _19_out, _29_out);
  or or_1 (w, _8_2_out, _9_2_out);
  or or_2 (x, _4_2_out, _5_2_out, _6_2_out, _7_2_out);
  or or_3 (y, _2_2_out, _3_2_out, _6_2_out, _7_2_out);
  or or_4 (z, _1_2_out, _3_2_out, _5_2_out, _7_2_out, _9_2_out);
endmodule
