// Logisim project looping_counter.circ as structural Verilog: 6 circuits, main circuit main_decimal
module main_decimal (
);

  wire CLOCK_out, dec_7seg_driver_1_a, dec_7seg_driver_1_b, dec_7seg_driver_1_c, dec_7seg_driver_1_d,
       dec_7seg_driver_1_e, dec_7seg_driver_1_f, dec_7seg_driver_1_g, dec_7seg_driver_2_a,
       dec_7seg_driver_2_b, dec_7seg_driver_2_c, dec_7seg_driver_2_d, dec_7seg_driver_2_e,
       dec_7seg_driver_2_f, dec_7seg_driver_2_g, dec_counter_1__0, dec_counter_1__1, dec_counter_1__2,
       dec_counter_1__3, dec_counter_2__0, dec_counter_2__1, dec_counter_2__2, dec_counter_2__3,
       dec_counter_2_is_nine;

  dec_7seg_driver dec_7seg_driver_1 (
    .w(dec_counter_1__3), .x(dec_counter_1__2), .y(dec_counter_1__1), .z(dec_counter_1__0),
    .a(dec_7seg_driver_1_a), .b(dec_7seg_driver_1_b), .c(dec_7seg_driver_1_c), .d(dec_7seg_driver_1_d),
    .e(dec_7seg_driver_1_e), .f(dec_7seg_driver_1_f), .g(dec_7seg_driver_1_g));
  dec_counter dec_counter_1 (
    .Clock(dec_counter_2_is_nine), ._0(dec_counter_1__0), ._1(dec_counter_1__1), ._2(dec_counter_1__2),
    ._3(dec_counter_1__3));  // open: IS_NINE
  _7_Segment_Display u_7_segment_display_1 (
    .g(dec_7seg_driver_1_g), .f(dec_7seg_driver_1_f), .a(dec_7seg_driver_1_a), .b(dec_7seg_driver_1_b),
    .e(dec_7seg_driver_1_e), .d(dec_7seg_driver_1_d), .c(dec_7seg_driver_1_c));  // open: dp
  Clock CLOCK (.out(CLOCK_out));
  dec_counter dec_counter_2 (
    .Clock(CLOCK_out), .IS_NINE(dec_counter_2_is_nine), ._0(dec_counter_2__0), ._1(dec_counter_2__1),
    ._2(dec_counter_2__2), ._3(dec_counter_2__3));
  dec_7seg_driver dec_7seg_driver_2 (
    .w(dec_counter_2__3), .x(dec_counter_2__2), .y(dec_counter_2__1), .z(dec_counter_2__0),
    .a(dec_7seg_driver_2_a), .b(dec_7seg_driver_2_b), .c(dec_7seg_driver_2_c), .d(dec_7seg_driver_2_d),
    .e(dec_7seg_driver_2_e), .f(dec_7seg_driver_2_f), .g(dec_7seg_driver_2_g));
  _7_Segment_Display u_7_segment_display_2 (
    .g(dec_7seg_driver_2_g), .f(dec_7seg_driver_2_f), .a(dec_7seg_driver_2_a), .b(dec_7seg_driver_2_b),
    .e(dec_7seg_driver_2_e), .d(dec_7seg_driver_2_d), .c(dec_7seg_driver_2_c));  // open: dp
endmodule

module main_hexadecimal (
);

  wire CLOCK_out, hex_7seg_driver_1_a, hex_7seg_driver_1_b, hex_7seg_driver_1_c, hex_7seg_driver_1_d,
       hex_7seg_driver_1_e, hex_7seg_driver_1_f, hex_7seg_driver_1_g, hex_7seg_driver_2_a,
       hex_7seg_driver_2_b, hex_7seg_driver_2_c, hex_7seg_driver_2_d, hex_7seg_driver_2_e,
       hex_7seg_driver_2_f, hex_7seg_driver_2_g, hex_counter_1__0, hex_counter_1__1, hex_counter_1__2,
       hex_counter_1__3, hex_counter_2__0, hex_counter_2__1, hex_counter_2__2, hex_counter_2__3,
       hex_counter_2_is_fifteen;

  hex_counter hex_counter_1 (
    .Clock(hex_counter_2_is_fifteen), ._0(hex_counter_1__0), ._1(hex_counter_1__1), ._2(hex_counter_1__2),
    ._3(hex_counter_1__3));  // open: IS_FIFTEEN
  hex_7seg_driver hex_7seg_driver_1 (
    .w(hex_counter_1__3), .x(hex_counter_1__2), .y(hex_counter_1__1), .z(hex_counter_1__0),
    .a(hex_7seg_driver_1_a), .b(hex_7seg_driver_1_b), .c(hex_7seg_driver_1_c), .d(hex_7seg_driver_1_d),
    .e(hex_7seg_driver_1_e), .f(hex_7seg_driver_1_f), .g(hex_7seg_driver_1_g));
  _7_Segment_Display u_7_segment_display_1 (
    .g(hex_7seg_driver_1_g), .f(hex_7seg_driver_1_f), .a(hex_7seg_driver_1_a), .b(hex_7seg_driver_1_b),
    .e(hex_7seg_driver_1_e), .d(hex_7seg_driver_1_d), .c(hex_7seg_driver_1_c));  // open: dp
  Clock CLOCK (.out(CLOCK_out));
  hex_counter hex_counter_2 (
    .Clock(CLOCK_out), .IS_FIFTEEN(hex_counter_2_is_fifteen), ._0(hex_counter_2__0), ._1(hex_counter_2__1),
    ._2(hex_counter_2__2), ._3(hex_counter_2__3));
  hex_7seg_driver hex_7seg_driver_2 (
    .w(hex_counter_2__3), .x(hex_counter_2__2), .y(hex_counter_2__1), .z(hex_counter_2__0),
    .a(hex_7seg_driver_2_a), .b(hex_7seg_driver_2_b), .c(hex_7seg_driver_2_c), .d(hex_7seg_driver_2_d),
    .e(hex_7seg_driver_2_e), .f(hex_7seg_driver_2_f), .g(hex_7seg_driver_2_g));
  _7_Segment_Display u_7_segment_display_2 (
    .g(hex_7seg_driver_2_g), .f(hex_7seg_driver_2_f), .a(hex_7seg_driver_2_a), .b(hex_7seg_driver_2_b),
    .e(hex_7seg_driver_2_e), .d(hex_7seg_driver_2_d), .c(hex_7seg_driver_2_c));  // open: dp
endmodule

module dec_7seg_driver (
  input  w,
  input  x,
  input  y,
  input  z,
  output a,
  output b,
  output c,
  output d,
  output e,
  output f,
  output g
);

  wire and_1_out, and_2_out, and_3_out, and_4_out, and_5_out, and_6_out, and_7_out, and_8_out, and_9_out,
       and_10_out, and_11_out, and_12_out, and_13_out, and_14_out, not_1_out, not_2_out, not_3_out, not_4_out;

  not not_1 (not_1_out, w);
  not not_2 (not_2_out, x);
  not not_3 (not_3_out, y);
  not not_4 (not_4_out, z);
  and and_1 (and_1_out, x, z);
  and and_2 (and_2_out, not_2_out, not_4_out);
  and and_3 (and_3_out, not_3_out, not_4_out);
  and and_4 (and_4_out, y, z);
  and and_5 (and_5_out, not_2_out, not_4_out);
  and and_6 (and_6_out, not_2_out, y);
  and and_7 (and_7_out, y, not_4_out);
  and and_8 (and_8_out, x, not_3_out, z);
  and and_9 (and_9_out, not_2_out, not_4_out);
  and and_10 (and_10_out, y, not_4_out);
  and and_11 (and_11_out, not_3_out, not_4_out);
  and and_12 (and_12_out, x, not_3_out);
  and and_13 (and_13_out, not_2_out, y);
  and and_14 (and_14_out, y, not_4_out);
  or or_1 (a, w, y, and_1_out, and_2_out);
  or or_2 (b, not_2_out, and_3_out, and_4_out);
  or or_3 (c, x, not_3_out, z);
  or or_4 (d, w, and_5_out, and_6_out, and_7_out, and_8_out);
  or or_5 (e, and_9_out, and_10_out);
  or or_6 (f, w, x, and_11_out);
  or or_7 (g, w, and_12_out, and_13_out, and_14_out);
endmodule

module dec_counter (
  input  Clock,
  output _0,
  output _1,
  output _2,
  output _3,
  output IS_NINE
);

  wire and_2_out, and_3_out, and_4_out, and_5_out, and_6_out, and_7_out, and_8_out, D1_qn, D2_qn, D3_qn,
       D4_qn, or_1_out, or_2_out, or_3_out;

  and and_1 (IS_NINE, _3, D2_qn, D3_qn, _0);
  and and_2 (and_2_out, _3, D4_qn);
  and and_3 (and_3_out, _2, _1, _0);
  and and_4 (and_4_out, _2, D3_qn);
  and and_5 (and_5_out, _2, D4_qn);
  and and_6 (and_6_out, D2_qn, _1, _0);
  and and_7 (and_7_out, _1, D4_qn);
  and and_8 (and_8_out, D1_qn, D3_qn, _0);
  or or_1 (or_1_out, and_2_out, and_3_out);
  or or_2 (or_2_out, and_4_out, and_5_out, and_6_out);
  or or_3 (or_3_out, and_7_out, and_8_out);
  D_Flip_Flop #(.trigger("falling")) D1 (.clk(Clock), .D(or_1_out), .Q(_3), .Qn(D1_qn));  // open: preset, en, reset
  D_Flip_Flop #(.trigger("falling")) D2 (.clk(Clock), .D(or_2_out), .Q(_2), .Qn(D2_qn));  // open: preset, en, reset
  D_Flip_Flop #(.trigger("falling")) D3 (.clk(Clock), .D(or_3_out), .Q(_1), .Qn(D3_qn));  // open: preset, en, reset
  D_Flip_Flop #(.trigger("falling")) D4 (.clk(Clock), .D(D4_qn), .Q(_0), .Qn(D4_qn));  // open: preset, en, reset
endmodule

module hex_7seg_driver (
  input  w,
  input  x,
  input  y,
  input  z,
  output a,
  output b,
  output c,
  output d,
  output e,
  output f,
  output g
);

  wire and_1_out, and_2_out, and_3_out, and_4_out, and_5_out, and_6_out, and_7_out, and_8_out, and_9_out,
       and_10_out, and_11_out, and_12_out, and_13_out, and_14_out, and_15_out, and_16_out, and_17_out,
       and_18_out, and_19_out, and_20_out, and_21_out, and_22_out, and_23_out, and_24_out, and_25_out,
       and_26_out, and_27_out, and_28_out, and_29_out, and_30_out, and_31_out, and_32_out, and_33_out,
       and_34_out, not_1_out, not_2_out, not_3_out, not_4_out;

  not not_1 (not_1_out, w);
  not not_2 (not_2_out, x);
  not not_3 (not_3_out, y);
  not not_4 (not_4_out, z);
  and and_1 (and_1_out, w, not_2_out, not_3_out);
  and and_2 (and_2_out, not_2_out, not_4_out);
  and and_3 (and_3_out, w, not_4_out);
  and and_4 (and_4_out, not_1_out, y);
  and and_5 (and_5_out, x, y);
  and and_6 (and_6_out, not_1_out, x, z);
  and and_7 (and_7_out, not_1_out, not_2_out);
  and and_8 (and_8_out, not_2_out, not_4_out);
  and and_9 (and_9_out, not_1_out, not_3_out, not_4_out);
  and and_10 (and_10_out, not_1_out, y, z);
  and and_11 (and_11_out, w, not_3_out, z);
  and and_12 (and_12_out, not_1_out, x);
  and and_13 (and_13_out, w, not_2_out);
  and and_14 (and_14_out, not_3_out, z);
  and and_15 (and_15_out, not_1_out, not_3_out);
  and and_16 (and_16_out, not_1_out, z);
  and and_17 (and_17_out, w, not_3_out);
  and and_18 (and_18_out, x, not_3_out, z);
  and and_19 (and_19_out, not_2_out, y, z);
  and and_20 (and_20_out, not_1_out, not_2_out, not_4_out);
  and and_21 (and_21_out, x, y, not_4_out);
  and and_22 (and_22_out, not_2_out, not_4_out);
  and and_23 (and_23_out, w, x);
  and and_24 (and_24_out, w, y);
  and and_25 (and_25_out, y, not_4_out);
  and and_26 (and_26_out, not_1_out, x);
  and and_27 (and_27_out, w, not_2_out);
  and and_28 (and_28_out, not_3_out, not_4_out);
  and and_29 (and_29_out, w, y);
  and and_30 (and_30_out, w, not_2_out);
  and and_31 (and_31_out, w, z);
  and and_32 (and_32_out, y, not_4_out);
  and and_33 (and_33_out, not_2_out, y);
  and and_34 (and_34_out, not_1_out, x, not_3_out);
  or or_1 (a, and_1_out, and_2_out, and_3_out, and_4_out, and_5_out, and_6_out);
  or or_2 (b, and_7_out, and_8_out, and_9_out, and_10_out, and_11_out);
  or or_3 (c, and_12_out, and_13_out, and_14_out, and_15_out, and_16_out);
  or or_4 (d, and_17_out, and_18_out, and_19_out, and_20_out, and_21_out);
  or or_5 (e, and_22_out, and_23_out, and_24_out, and_25_out);
  or or_6 (f, and_26_out, and_27_out, and_28_out, and_29_out);
  or or_7 (g, and_30_out, and_31_out, and_32_out, and_33_out, and_34_out);
endmodule

module hex_counter (
  input  Clock,
  output _0,
  output _1,
  output _2,
  output _3,
  output IS_FIFTEEN
);

  wire and_2_out, and_3_out, and_4_out, and_5_out, and_6_out, and_7_out, and_8_out, and_9_out, and_10_out,
       D1_qn, D2_qn, D3_qn, D4_qn, or_1_out, or_2_out, or_3_out;

  and and_1 (IS_FIFTEEN, _3, _2, _1, _0);
  and and_2 (and_2_out, _3, D2_qn);
  and and_3 (and_3_out, _3, D3_qn);
  and and_4 (and_4_out, _3, D4_qn);
  and and_5 (and_5_out, D1_qn, _2, _1, _0);
  and and_6 (and_6_out, _2, D3_qn);
  and and_7 (and_7_out, _2, D4_qn);
  and and_8 (and_8_out, D2_qn, _1, _0);
  and and_9 (and_9_out, _1, D4_qn);
  and and_10 (and_10_out, D3_qn, _0);
  or or_1 (or_1_out, and_2_out, and_3_out, and_4_out, and_5_out);
  or or_2 (or_2_out, and_6_out, and_7_out, and_8_out);
  or or_3 (or_3_out, and_9_out, and_10_out);
  D_Flip_Flop #(.trigger("falling")) D1 (.clk(Clock), .D(or_1_out), .Q(_3), .Qn(D1_qn));  // open: preset, en, reset
  D_Flip_Flop #(.trigger("falling")) D2 (.clk(Clock), .D(or_2_out), .Q(_2), .Qn(D2_qn));  // open: preset, en, reset
  D_Flip_Flop #(.trigger("falling")) D3 (.clk(Clock), .D(or_3_out), .Q(_1), .Qn(D3_qn));  // open: preset, en, reset
  D_Flip_Flop #(.trigger("falling")) D4 (.clk(Clock), .D(D4_qn), .Q(_0), .Qn(D4_qn));  // open: preset, en, reset
endmodule
